# Fritzing sketch SherlockSketch (saved by Fritzing 0.9.3b)
circuit board: 8.46667cm x 5.64444cm
breadboards: 1

parts:
  Raspberry_Pi_1 = Raspberry Pi 3 [part_number=RPI-3-V1.2]
  R1 = Resistor [tolerance=±5% resistance=220 package=THT]
  LED1 = LED - 5mm [color="Green (570nm)" package="5 mm [THT]"]
  R2 = TRIMPOT [package=trimpot_pth_s3_lock]
  ADC1 = MCP3008 [package=dil16]
  S1 = Pushbutton [package="[THT]"]
  Power_plug1 = Power plug  # not connected
  S2 = Pushbutton [package="[THT]"]
  S3 = Pushbutton [package="[THT]"]
  R3 = Resistor [tolerance=±5% resistance=220 package=THT]
  R4 = Resistor [tolerance=±5% resistance=220 package=THT]
  R5 = Resistor [tolerance=±5% resistance=220 package=THT]

nets:
  N1: Raspberry_Pi_1.GPIO2, S3.Pin_1, S3.Pin_2, R5.Pin_1
  N2: Raspberry_Pi_1.GPIO3, S1.Pin_1, S1.Pin_2, R3.Pin_1
  N3: Raspberry_Pi_1.GND, LED1.cathode, R2.CW, ADC1.CH0, ADC1.CH5, S1.Pin_3, S1.Pin_4, S2.Pin_3, S2.Pin_4, S3.Pin_3, S3.Pin_4
  N4: Raspberry_Pi_1.GPIO17, S2.Pin_1, S2.Pin_2, R4.Pin_1
  N5: Raspberry_Pi_1.GPIO27, R1.Pin_0
  N6: Raspberry_Pi_1.GPIO10, ADC1.CH2
  N7: Raspberry_Pi_1.GPIO9, ADC1.CH3
  N8: Raspberry_Pi_1.GPIO11, ADC1.CH4
  N9: Raspberry_Pi_1.GPIO8, ADC1.CH1
  N10: Raspberry_Pi_1.5V, R2.CCW, ADC1.CH6, ADC1.CH7, R3.Pin_0, R4.Pin_0, R5.Pin_0
  N11: R1.Pin_1, LED1.anode
  N12: R2.WIPER, ADC1.DGND

notes:
  BACK
  PAUSE
  NEXT
  VOLUME
  LED ON/OFF
  AUDIO
