# Fritzing sketch Sherlock_dev_sketch (saved by Fritzing 0.9.3b)
breadboards: 1

parts:
  Raspberry_Pi_1 = Raspberry Pi 3 [part_number=RPI-3-V1.2]
  LED1 = LED - 5mm [color="Red (633nm)" package="5 mm [THT]"]
  LED2 = LED - 5mm [color="Red (633nm)" package="5 mm [THT]"]
  LED3 = LED - 5mm [color="Red (633nm)" package="5 mm [THT]"]
  R1 = Resistor [tolerance=±5% resistance=220 package=THT]
  R2 = Resistor [tolerance=±5% resistance=220 package=THT]
  R3 = Resistor [tolerance=±5% resistance=220 package=THT]
  Q1 = MOSFET-NCHANNEL [package=to-92]
  Q2 = MOSFET-NCHANNEL [package=to-92]
  Q3 = MOSFET-NCHANNEL [package=to-92]
  S1 = SWITCH-MOMENTARY-2 [package=tactile_switch_tall]
  S3 = SWITCH-MOMENTARY-2 [package=tactile_switch_tall]
  S2 = SWITCH-MOMENTARY-2 [package=tactile_switch_tall]

nets:
  N1: Raspberry_Pi_1.GPIO4, S1.2
  N2: Raspberry_Pi_1.GPIO27, Q3.D
  N3: Raspberry_Pi_1.GPIO13, Q2.D
  N4: Raspberry_Pi_1.GND, Q2.S, Q3.S, S3.1
  N5: Raspberry_Pi_1.GPIO16, Q1.D
  N6: Raspberry_Pi_1.GPIO12, LED3.anode
  N7: Raspberry_Pi_1.GPIO24, LED2.anode
  N8: Raspberry_Pi_1.GPIO23, LED1.anode
  N9: LED1.cathode, R1.Pin_0
  N10: LED2.cathode, R2.Pin_0
  N11: LED3.cathode, R3.Pin_0
  GND: R1.Pin_1, R2.Pin_1, R3.Pin_1, Q1.S, S1.1, S2.1
